// Digital circuit q-clock-v2.dig as structural Verilog
module q_clock_v2 (
  input  Scan,
  input  Clock,
  input  BRK,
  output Inverted,
  output Primary
);

  wire and_1_out, Auto_out, d_ff_1_q, d_ff_2_nq, d_ff_2_q, d_ff_3_nq, d_ff_3_q, d_ff_4_nq, d_ff_4_q,
       Manual_out, multiplexer_1_out, multiplexer_2_out, not_1_out, not_2_out, or_1_out, xor_1_out;

  Button Auto (.out(Auto_out));
  Button Manual (.out(Manual_out));
  PullDown pulldown_1 (.out(Manual_out));
  D_FF d_ff_1 (.D(Manual_out), .C(Scan), .Q(d_ff_1_q));  // open: nQ
  not not_1 (not_1_out, Clock);
  or or_1 (or_1_out, Auto_out, and_1_out);
  and and_1 (and_1_out, multiplexer_2_out, d_ff_3_q);
  D_FF d_ff_2 (.D(d_ff_1_q), .C(Scan), .Q(d_ff_2_q), .nQ(d_ff_2_nq));
  D_FF d_ff_3 (.D(or_1_out), .C(not_1_out), .Q(d_ff_3_q), .nQ(d_ff_3_nq));
  xor xor_1 (xor_1_out, d_ff_1_q, d_ff_2_q);
  Multiplexer multiplexer_1 (.sel(d_ff_3_nq), .in_0(Clock), .in_1(xor_1_out), .out(multiplexer_1_out));
  Multiplexer multiplexer_2 (.sel(d_ff_4_nq), .in_0(d_ff_2_nq), .in_1(BRK), .out(multiplexer_2_out));
  not not_2 (not_2_out, multiplexer_1_out);
  D_FF d_ff_4 (.D(d_ff_4_nq), .C(not_2_out), .Q(d_ff_4_q), .nQ(d_ff_4_nq));
  nor nor_1 (Inverted, not_2_out, d_ff_4_q);
  nor nor_2 (Primary, d_ff_4_nq, not_2_out);

  // Notes on the sheet:
  //   Clock: Hz: 2
  //   BRK: default 1
endmodule
